# Fritzing sketch fritzing (saved by Fritzing 0.9.3b)
breadboards: 1

parts:
  Componente1 = Arduino Uno (Rev3)
  R1 = Resistor [tolerance=±5% resistance=220 package=THT]
  S1 = Pushbutton [package="[THT]"]  # not connected
  J1 = Basic Servo

nets:
  N1: Componente1.D9_PWM, J1.pulse
  N2: Componente1.D2, R1.Pin_1
  5V: Componente1.5V, J1.vcc
  GND: Componente1.GND, R1.Pin_0, J1.gnd
