# Fritzing sketch fritzing (saved by Fritzing 0.9.3b)
breadboards: 1

parts:
  Componente1 = Arduino Uno (Rev3)
  LED2 = smd LED [color="Green (565nm)" package="0603 [SMD]"]
  LED3 = smd LED [color="Red (633nm)" package="0603 [SMD]"]
  J1 = Piezo Speaker
  R1 = Resistor [tolerance=±5% resistance=220 package="2010 [SMD]"]
  R2 = Resistor [tolerance=±5% resistance=220 package="2010 [SMD]"]

nets:
  N1: Componente1.D11_PWM/MOSI, J1.pin2
  N2: Componente1.D12/MISO, LED2.anode
  N3: Componente1.D13/SCK, LED3.anode
  N4: Componente1.GND, J1.pin1, R1.Pin_1, R2.Pin_1
  N5: LED2.cathode, R2.Pin_0
  N6: LED3.cathode, R1.Pin_0
