# Fritzing sketch fritzing (saved by Fritzing 0.9.3b)
breadboards: 1

parts:
  Componente1 = Arduino Uno (Rev3)
  R1 = Resistor [tolerance=±5% resistance=220 package=THT]
  LED1 = LED - 5mm [color="Red (633nm)" package="5 mm [THT]"]
  R2 = Photocell (LDR) [package=THT]
  R3 = Resistor [tolerance=±5% resistance=10k package=THT]
  J1 = Basic Servo  # not connected

nets:
  N1: Componente1.A0, R2.pin_1, R3.Pin_0
  N2: Componente1.D13/SCK, LED1.cathode
  N3: Componente1.5V, R2.pin_0
  N4: R1.Pin_0, LED1.anode
  N5: R1.Pin_1, R3.Pin_1
