# Fritzing sketch fritzing (saved by Fritzing 0.9.3b)
breadboards: 1

parts:
  LED1 = LED - 5mm [color="Red (633nm)" package="5 mm [THT]"]
  LED2 = LED - 5mm [color="Green (565nm)" package="5 mm [THT]"]
  Componente1 = Arduino Uno (Rev3)
  R1 = Resistor [tolerance=±5% resistance=220 package=THT]
  R2 = Resistor [tolerance=±5% resistance=220 package=THT]

nets:
  N1: LED1.cathode, R1.Pin_1
  N2: LED1.anode, Componente1.D10_PWM/SS
  N3: LED2.cathode, R2.Pin_1
  N4: LED2.anode, Componente1.D9_PWM
  N5: Componente1.GND, R1.Pin_0, R2.Pin_0
